# Fritzing sketch temp-tracker-schematic (saved by Fritzing 0.7.11b)
breadboards: 1

parts:
  Arduino_Ethernet_Shield1 = Arduino Ethernet Shield
  T1 = LM35 Temperature Sensor [package="TO92 [THT]"]

nets:
  N1: Arduino_Ethernet_Shield1.aref, Arduino_Ethernet_Shield1.3V3, T1.+Vs
  N2: Arduino_Ethernet_Shield1.D0RX, T1.Vout
  GND: Arduino_Ethernet_Shield1.GND, T1.GND

notes:
  3.3V
  GND
  Important! The flat side of the TMP36 must be facing the Arduino
